# Fritzing sketch Schematic (saved by Fritzing 0.9.3b)
breadboards: 1

parts:
  Raspberry_Pi_1 = Raspberry Pi 3 [part_number=RPI-3-V1.2]
  IC1 = IC, DIP package, 8 pins [chip_label=IC]
  J1 = Piezo Speaker
  S1 = Pushbutton [package="[THT]"]
  S2 = Pushbutton [package="[THT]"]

nets:
  N1: Raspberry_Pi_1.3v3, IC1.pin1
  N2: Raspberry_Pi_1.GPIO10, IC1.pin4
  N3: Raspberry_Pi_1.GPIO9, IC1.pin3
  N4: Raspberry_Pi_1.GPIO5, S1.Pin_3, S1.Pin_4
  N5: Raspberry_Pi_1.GPIO13, S2.Pin_3, S2.Pin_4
  N6: Raspberry_Pi_1.GPIO25, IC1.pin2
  N7: Raspberry_Pi_1.GND, IC1.pin7, J1.pin1, S1.Pin_1, S1.Pin_2, S2.Pin_1, S2.Pin_2
  N8: IC1.pin8, J1.pin2
